// Logisim project alu.circ as structural Verilog: 9 circuits, main circuit alumain
module alumain (
  input  [31:0] A,
  input  [31:0] B,
  input  [3:0] ALUSel,
  output OverFlow,
  output Zero,
  output [31:0] Result
);

  wire l_1st_sub_7389c877_1_overflow, nor_1_out, orallbits_1_out_2;
  wire [31:0] l_1st_sub_7389c877_1_l_1_cd6b56be, l_1st_sub_7389c877_1_l_2_74f565d6,
       l_1st_sub_7389c877_1_l_3_a6a6c12a, l_1st_sub_7389c877_1_l_4_e180b91f,
       l_2nd_sub_c086d1b5_1_l_1_cd6b56be, l_2nd_sub_c086d1b5_1_l_2_74f565d6,
       l_2nd_sub_c086d1b5_1_l_3_a6a6c12a, l_2nd_sub_c086d1b5_1_l_4_e180b91f,
       l_3rd_sub_95b81e40_1_l_1_cd6b56be, l_3rd_sub_95b81e40_1_l_2_74f565d6,
       l_3rd_sub_95b81e40_1_l_3_a6a6c12a, l_3rd_sub_95b81e40_1_l_4_e180b91f,
       l_4th_sub_e368a1ee_1_l_1_cd6b56be, l_4th_sub_e368a1ee_1_l_2_74f565d6,
       l_4th_sub_e368a1ee_1_l_3_a6a6c12a, l_4th_sub_e368a1ee_1_l_4_e180b91f;

  L_3rd_Sub_95b81e40 l_3rd_sub_95b81e40_1 (
    .A(A), .B(B), .L_1_cd6b56be(l_3rd_sub_95b81e40_1_l_1_cd6b56be),
    .L_2_74f565d6(l_3rd_sub_95b81e40_1_l_2_74f565d6), .L_3_a6a6c12a(l_3rd_sub_95b81e40_1_l_3_a6a6c12a),
    .L_4_e180b91f(l_3rd_sub_95b81e40_1_l_4_e180b91f));
  L_1st_Sub_7389c877 l_1st_sub_7389c877_1 (
    .A(A), .B(B), .L_1_cd6b56be(l_1st_sub_7389c877_1_l_1_cd6b56be),
    .L_2_74f565d6(l_1st_sub_7389c877_1_l_2_74f565d6), .L_3_a6a6c12a(l_1st_sub_7389c877_1_l_3_a6a6c12a),
    .L_4_e180b91f(l_1st_sub_7389c877_1_l_4_e180b91f), .OverFlow(l_1st_sub_7389c877_1_overflow));
  L_2nd_Sub_c086d1b5 l_2nd_sub_c086d1b5_1 (
    .A(A), .B(B), .L_1_cd6b56be(l_2nd_sub_c086d1b5_1_l_1_cd6b56be),
    .L_2_74f565d6(l_2nd_sub_c086d1b5_1_l_2_74f565d6), .L_3_a6a6c12a(l_2nd_sub_c086d1b5_1_l_3_a6a6c12a),
    .L_4_e180b91f(l_2nd_sub_c086d1b5_1_l_4_e180b91f));
  L_4th_Sub_e368a1ee l_4th_sub_e368a1ee_1 (
    .A(A), .B(B), .L_1_cd6b56be(l_4th_sub_e368a1ee_1_l_1_cd6b56be),
    .L_2_74f565d6(l_4th_sub_e368a1ee_1_l_2_74f565d6), .L_3_a6a6c12a(l_4th_sub_e368a1ee_1_l_3_a6a6c12a),
    .L_4_e180b91f(l_4th_sub_e368a1ee_1_l_4_e180b91f));
  Multiplexer #(.select(4), .width(32)) multiplexer_1 (
    .in0(l_1st_sub_7389c877_1_l_1_cd6b56be), .in1(l_1st_sub_7389c877_1_l_2_74f565d6),
    .in2(l_1st_sub_7389c877_1_l_3_a6a6c12a), .in3(l_1st_sub_7389c877_1_l_4_e180b91f),
    .in4(l_2nd_sub_c086d1b5_1_l_1_cd6b56be), .in5(l_2nd_sub_c086d1b5_1_l_2_74f565d6),
    .in6(l_2nd_sub_c086d1b5_1_l_3_a6a6c12a), .in7(l_2nd_sub_c086d1b5_1_l_4_e180b91f),
    .in8(l_3rd_sub_95b81e40_1_l_1_cd6b56be), .in9(l_3rd_sub_95b81e40_1_l_2_74f565d6),
    .in10(l_3rd_sub_95b81e40_1_l_3_a6a6c12a), .in11(l_3rd_sub_95b81e40_1_l_4_e180b91f),
    .in12(l_4th_sub_e368a1ee_1_l_1_cd6b56be), .in13(l_4th_sub_e368a1ee_1_l_2_74f565d6),
    .in14(l_4th_sub_e368a1ee_1_l_3_a6a6c12a), .in15(l_4th_sub_e368a1ee_1_l_4_e180b91f), .out(Result),
    .sel(ALUSel));
  nor nor_1 (nor_1_out, ALUSel[2], ALUSel[3], ALUSel[1], ALUSel[0]);
  OrAllBits orallbits_1 (.in_1(Result), .out_2(orallbits_1_out_2));
  and and_1 (OverFlow, l_1st_sub_7389c877_1_overflow, nor_1_out);
  not not_1 (Zero, orallbits_1_out_2);
endmodule

module L_2nd_Sub_c086d1b5 (
  input  [31:0] A,
  input  [31:0] B,
  output [31:0] L_1_cd6b56be,
  output [31:0] L_2_74f565d6,
  output [31:0] L_3_a6a6c12a,
  output [31:0] L_4_e180b91f
);

  Shifter #(.shift("lr"), .width(32)) shifter_1 (.in(A), .\dist (B[4:0]), .out(L_2_74f565d6));
  assign L_1_cd6b56be = A ^ B;  // XOR_Gate xor_1, 32 bits wide
  assign L_3_a6a6c12a = A | B;  // OR_Gate or_1, 32 bits wide
  assign L_4_e180b91f = A & B;  // AND_Gate and_1, 32 bits wide
endmodule

module L_1st_Sub_7389c877 (
  input  [31:0] A,
  input  [31:0] B,
  output [31:0] L_1_cd6b56be,
  output OverFlow,
  output [31:0] L_2_74f565d6,
  output [31:0] L_3_a6a6c12a,
  output [31:0] L_4_e180b91f
);

  wire comparator_1_lt, comparator_2_lt, xor_1_out, xor_2_out;

  Adder #(.width(32)) adder_1 (.a(A), .b(B), .out(L_1_cd6b56be));  // open: cin, cout
  Shifter #(.width(32)) shifter_1 (.in(A), .\dist (B[4:0]), .out(L_2_74f565d6));
  Comparator #(.width(32)) comparator_1 (.a(A), .b(B), .lt(comparator_1_lt));  // open: gt, eq
  Comparator #(.mode("unsigned"), .width(32)) comparator_2 (.a(A), .b(B), .lt(comparator_2_lt));  // open: gt, eq
  assign L_3_a6a6c12a = {{31{1'b0}}, comparator_1_lt};  // Bit_Extender bit_extender_1
  assign L_4_e180b91f = {{31{1'b0}}, comparator_2_lt};  // Bit_Extender bit_extender_2
  xor xor_1 (xor_1_out, A[31], L_1_cd6b56be[31]);
  xor xor_2 (xor_2_out, L_1_cd6b56be[31], B[31]);
  and and_1 (OverFlow, xor_1_out, xor_2_out);
endmodule

module L_3rd_Sub_95b81e40 (
  input  [31:0] A,
  input  [31:0] B,
  output [31:0] L_1_cd6b56be,
  output [31:0] L_2_74f565d6,
  output [31:0] L_3_a6a6c12a,
  output [31:0] L_4_e180b91f
);

  Multiplier #(.mode("twosComplement"), .width(32)) multiplier_1 (
    .a(A), .b(B), .out(L_1_cd6b56be), .cout(L_2_74f565d6));  // open: cin
  UnsignedMult unsignedmult_1 (.in_1(A), .in_2(B), .out_3(L_4_e180b91f));

  assign L_3_a6a6c12a = {32{1'b0}};
endmodule

module L_4th_Sub_e368a1ee (
  input  [31:0] A,
  input  [31:0] B,
  output [31:0] L_1_cd6b56be,
  output [31:0] L_2_74f565d6,
  output [31:0] L_3_a6a6c12a,
  output [31:0] L_4_e180b91f
);

  Shifter #(.shift("ar"), .width(32)) shifter_1 (.in(A), .\dist (B[4:0]), .out(L_2_74f565d6));
  Subtractor #(.width(32)) subtractor_1 (.a(A), .b(B), .out(L_1_cd6b56be));  // open: bin, bout

  assign L_3_a6a6c12a = {32{1'b0}};
  assign L_4_e180b91f = B;
endmodule

module L_4to1MUX_dffa73f4 (
  input  [31:0] L_1_cd6b56be,
  input  [31:0] L_2_74f565d6,
  input  [31:0] L_3_a6a6c12a,
  input  [31:0] L_4_e180b91f,
  input  S1,
  input  S0,
  output [31:0] Out
);

  Multiplexer #(.select(2), .width(32)) multiplexer_1 (
    .in0(L_1_cd6b56be), .in1(L_2_74f565d6), .in2(L_3_a6a6c12a), .in3(L_4_e180b91f), .out(Out), .sel({S1, S0}));
endmodule

// 16:1 MUX
module L_16to1MUX_2795e750 (
  input  [31:0] in_1,
  input  [31:0] in_2,
  input  [31:0] in_3,
  input  [31:0] in_4,
  input  [31:0] in_5,
  input  [31:0] in_6,
  input  [31:0] in_7,
  input  [31:0] in_8,
  input  [31:0] in_9,
  input  [31:0] in_10,
  input  [31:0] in_11,
  input  [31:0] in_12,
  input  [31:0] in_13,
  input  [31:0] in_14,
  input  [31:0] in_15,
  input  [31:0] in_16,
  input  [3:0] in_17,
  output [31:0] out_18
);

  Multiplexer #(.select(4), .width(32)) multiplexer_1 (
    .in0(in_1), .in1(in_2), .in2(in_3), .in3(in_4), .in4(in_5), .in5(in_6), .in6(in_7), .in7(in_8),
    .in8(in_9), .in9(in_10), .in10(in_11), .in11(in_12), .in12(in_13), .out(out_18));  // open: in13, in14, in15, sel
endmodule

module UnsignedMult (
  input  [31:0] in_1,
  input  [31:0] in_2,
  output [31:0] out_3
);

  wire adder_1_cout, adder_3_cout;
  wire [31:0] adder_1_out, adder_2_out, bit_extender_1_out, bit_extender_2_out, bit_extender_3_out,
       bit_extender_4_out, multiplier_1_out, multiplier_2_cout, multiplier_2_out, multiplier_3_out,
       shifter_1_out, shifter_2_out, shifter_3_out, shifter_4_out, shifter_5_out;

  assign bit_extender_1_out = {{31{in_1[0]}}, in_1[0]};  // Bit_Extender bit_extender_1
  assign bit_extender_2_out = {{1{in_1[31]}}, in_1[31:1]};  // Bit_Extender bit_extender_2
  assign bit_extender_3_out = {{1{in_2[31]}}, in_2[31:1]};  // Bit_Extender bit_extender_3
  assign bit_extender_4_out = {{31{in_2[0]}}, in_2[0]};  // Bit_Extender bit_extender_4
  Multiplier #(.width(32)) multiplier_1 (
    .a(bit_extender_1_out), .b(bit_extender_3_out), .out(multiplier_1_out));  // open: cin, cout
  Multiplier #(.width(32)) multiplier_2 (
    .a(bit_extender_2_out), .b(bit_extender_3_out), .out(multiplier_2_out), .cout(multiplier_2_cout));  // open: cin
  Multiplier #(.width(32)) multiplier_3 (
    .a(bit_extender_2_out), .b(bit_extender_4_out), .out(multiplier_3_out));  // open: cin, cout
  Shifter #(.width(32)) shifter_1 (.in(multiplier_1_out), .\dist (5'b00001), .out(shifter_1_out));
  Shifter #(.width(32)) shifter_2 (.in(multiplier_2_out), .\dist (5'b00010), .out(shifter_2_out));
  Shifter #(.width(32)) shifter_3 (.in(multiplier_3_out), .\dist (5'b00001), .out(shifter_3_out));
  Shifter #(.shift("lr"), .width(32)) shifter_4 (.in(multiplier_2_out), .\dist (5'b11110), .out(shifter_4_out));
  Shifter #(.width(32)) shifter_5 (.in(multiplier_2_cout), .\dist (5'b00010), .out(shifter_5_out));
  Adder #(.width(32)) adder_1 (
    .a(shifter_1_out), .b(shifter_3_out), .out(adder_1_out), .cout(adder_1_cout));  // open: cin
  Adder #(.width(32)) adder_2 (
    .a(shifter_4_out), .b(shifter_5_out), .out(adder_2_out), .cin(adder_3_cout));  // open: cout
  Adder #(.width(32)) adder_3 (.a(adder_1_out), .b(shifter_2_out), .cout(adder_3_cout));  // open: out, cin
  Adder #(.width(32)) adder_4 (.a({32{1'b0}}), .b(adder_2_out), .out(out_3), .cin(adder_1_cout));  // open: cout
endmodule

// OR
module OrAllBits (
  input  [31:0] in_1,
  output out_2
);

  or or_1 (out_2, in_1[31], in_1[30], in_1[29], in_1[28], in_1[27], in_1[26], in_1[25], in_1[24], in_1[23], in_1[22], in_1[21], in_1[20], in_1[19], in_1[18], in_1[17], in_1[16], in_1[14], in_1[13], in_1[12], in_1[11], in_1[10], in_1[9], in_1[8], in_1[7], in_1[6], in_1[5], in_1[4], in_1[3], in_1[2], in_1[1], in_1[0], in_1[15]);
endmodule
