// Logisim project cpu.circ as structural Verilog: 5 circuits, main circuit main
module main (
  input  reset,
  input  in_2,
  output [31:0] op1,
  output [31:0] op2,
  output [31:0] res,
  output regclk,
  output [31:0] Instr,
  output [23:0] Addr,
  output [31:0] Imm,
  output [4:0] rd,
  output [3:0] ALUSel,
  output [4:0] rs1,
  output [4:0] rs2,
  output write
);

  wire alumain_1_zero, and_1_out, decodemain_1_alusrc, decodemain_1_branch, decodemain_1_memread,
       decodemain_1_memtoreg, decodemain_1_memwrite;
  wire [31:0] adder_1_out, adder_2_out, bit_extender_1_out, dmem_1_dout, multiplexer_1_out,
       regmain_1_readdata2, wrreg;

  PC pc_1 (.in_2(in_2), .in_1(multiplexer_1_out), .in_3(reset), .out_4(Addr));
  assign bit_extender_1_out = {{8{1'b0}}, Addr};  // Bit_Extender bit_extender_1
  Multiplexer #(.width(32)) multiplexer_1 (
    .in0(adder_1_out), .in1(adder_2_out), .out(multiplexer_1_out), .sel(and_1_out));
  Adder #(.width(32)) adder_1 (.a(bit_extender_1_out), .b(32'h4), .out(adder_1_out));  // open: cin, cout
  IMem imem_1 (.Addr(Addr), .Instr(Instr));
  decodemain decodemain_1 (
    .in_1(Instr), .rs1(rs1), .rs2(rs2), .Branch(decodemain_1_branch), .MemWrite(decodemain_1_memwrite),
    .MemRead(decodemain_1_memread), .RegWrite(write), .MemtoReg(decodemain_1_memtoreg),
    .ALUSrc(decodemain_1_alusrc), .rd(rd), .Immediate(Imm), .ALUSel(ALUSel));
  Adder #(.width(32)) adder_2 (.a(bit_extender_1_out), .b(Imm), .out(adder_2_out));  // open: cin, cout
  and and_1 (and_1_out, alumain_1_zero, decodemain_1_branch);
  regmain regmain_1 (
    .ReadRegister1_rs1(rs1), .ReadRegister2_rs2(rs2), .write(write), .Clk(in_2), .WriteData(wrreg),
    .WriteRegister_rd(rd), .ReadData1(op1), .ReadData2(regmain_1_readdata2));
  Multiplexer #(.width(32)) multiplexer_2 (.in0(regmain_1_readdata2), .in1(Imm), .out(op2), .sel(decodemain_1_alusrc));
  alumain alumain_1 (.A(op1), .B(op2), .ALUSel(ALUSel), .Result(res), .Zero(alumain_1_zero));  // open: OverFlow
  DMem dmem_1 (.Addr(res), .Din(regmain_1_readdata2), .Clk(in_2), .We(decodemain_1_memwrite), .Dout(dmem_1_dout));
  Multiplexer #(.width(32)) multiplexer_3 (.in0(res), .in1(dmem_1_dout), .out(wrreg), .sel(decodemain_1_memtoreg));

  assign regclk = in_2;

  // Other names for the same wires on the sheet: clk = in_2
endmodule

module DMem (
  input  [31:0] Addr,
  input  We,
  input  [31:0] Din,
  input  Clk,
  output [31:0] Dout
);

  // RAM #(.addrWidth(24), .enables("line"), .line("quad")) ram_1: pin names not known; wires that end beside it: Addr[23:0], We, 1'b1, 1'b1, 1'b1, 1'b1, Clk
endmodule

module IMem (
  input  [23:0] Addr,
  output [31:0] Instr
);

  // ROM #(.addrWidth(24), .line("quad")) rom_1: pin names not known; wires that end beside it: Addr

  // Notes on the sheet:
  //   contents of rom_1 (hex, n*v repeats v):
  //   13 5 15 0 63 4 a5 0 13 5 15 0 13 5 15 0 23 22 a1 0 83 24 41
endmodule

module PC (
  input  [31:0] in_1,
  input  in_2,
  input  in_3,
  output [23:0] out_4
);

  wire [31:24] register_1_q;

  Register #(.width(32)) register_1 (.D(in_1), .en(1'b1), .clk(in_2), .Q({register_1_q, out_4}), .clr(in_3));
endmodule

module clck (
  input  reset
);

  wire clk_out;

  Clock clk (.out(clk_out));
  // main main_1: pin names not known; wires that end beside it: reset, clk_out
endmodule
