// Logisim project decode.circ as structural Verilog: 1 circuit, main circuit decodemain
module decodemain (
  input  [31:0] in_1,
  output [4:0] rd,
  output Branch,
  output [3:0] ALUSel,
  output MemWrite,
  output MemRead,
  output RegWrite,
  output MemtoReg,
  output ALUSrc,
  output [31:0] Immediate,
  output [4:0] rs1,
  output [4:0] rs2
);

  wire [1:0] Sel;

  // PlaRom #(.Contents("1 2 2 1*4 2 1 2 2 1*3 2 0 0 1 0*5 1*4 0*3 1 1 0*3 1 0 1 0*6 1*4 0 1 0*4 1"), .\and (5), .outputs(8)) plarom_1: pin names not known; wires that end beside it: in_1[6:4], {ALUSrc, MemtoReg, RegWrite, MemRead, MemWrite, Branch, Sel}
  // PlaRom #(.Contents("1 2 2 1 2 0 0 1 1 2 0 2 0 0 1 2 2 1 0 2 0 1 1 2 0 0 2 0 1 2 2 1 0 0 2 1 1 2 0*3 2*3 1 0*4 1 2*3 0*3 0 1 0*3 1 0*4 1 0*3 1 0*4 1 0*3 1*3 0 0 1 1 0 0"), .\and (8)) plarom_2: pin names not known; wires that end beside it: {in_1[6:4], in_1[30], in_1[14:12]}, ALUSel
  Multiplexer #(.select(2)) multiplexer_1 (
    .in1(in_1[20]), .in2(in_1[7]), .in3(1'b0), .out(Immediate[0]), .sel(Sel));  // open: in0
  Multiplexer #(.select(2)) multiplexer_2 (
    .in1(in_1[21]), .in2(in_1[8]), .in3(in_1[8]), .out(Immediate[1]), .sel(Sel));  // open: in0
  Multiplexer #(.select(2)) multiplexer_3 (
    .in1(in_1[22]), .in2(in_1[9]), .in3(in_1[9]), .out(Immediate[2]), .sel(Sel));  // open: in0
  Multiplexer #(.select(2)) multiplexer_4 (
    .in1(in_1[23]), .in2(in_1[10]), .in3(in_1[10]), .out(Immediate[3]), .sel(Sel));  // open: in0
  Multiplexer #(.select(2)) multiplexer_5 (
    .in1(in_1[24]), .in2(in_1[11]), .in3(in_1[11]), .out(Immediate[4]), .sel(Sel));  // open: in0
  Multiplexer #(.select(2)) multiplexer_6 (
    .in1(in_1[31]), .in2(in_1[31]), .in3(in_1[7]), .out(Immediate[11]), .sel(Sel));  // open: in0

  assign {Immediate[31:12], Immediate[10:5]} = {{20{in_1[31]}}, in_1[30:25]};
  assign rd = in_1[11:7];
  assign rs1 = in_1[19:15];
  assign rs2 = in_1[24:20];

  // Other names for the same wires on the sheet: i0 = Immediate[0]; i1 = Immediate[1]; i2 = Immediate[2];
  //   i3 = Immediate[3]; i4 = Immediate[4]; i11 = Immediate[11]
endmodule
