// Logisim project register.circ as structural Verilog: 1 circuit, main circuit regmain
module regmain (
  input  [4:0] ReadRegister1_rs1,
  input  [4:0] WriteRegister_rd,
  input  write,
  input  Clk,
  input  [4:0] ReadRegister2_rs2,
  input  [31:0] WriteData,
  output [31:0] ReadData1,
  output [31:0] ReadData2
);

  wire demultiplexer_1_out1, demultiplexer_1_out2, demultiplexer_1_out5, demultiplexer_1_out6,
       demultiplexer_1_out7, demultiplexer_1_out8, demultiplexer_1_out9, demultiplexer_1_out10;
  wire [31:0] register_1_q, register_2_q, register_3_q, register_4_q, register_5_q, register_6_q,
       register_7_q, register_8_q, register_9_q;

  Demultiplexer #(.select(5)) demultiplexer_1 (
    .out1(demultiplexer_1_out1), .out2(demultiplexer_1_out2), .out5(demultiplexer_1_out5),
    .out6(demultiplexer_1_out6), .out7(demultiplexer_1_out7), .out8(demultiplexer_1_out8),
    .out9(demultiplexer_1_out9), .out10(demultiplexer_1_out10), .in(write), .sel(WriteRegister_rd));  // open: out0, out3, out4, out11, out12, out13, out14, out15, out16, out17, out18, out19, out20, out21, out22, out23, out24, out25, out26, out27, out28, out29, out30, out31
  Register #(.width(32)) register_1 (.D(WriteData), .en(1'b0), .clk(Clk), .Q(register_1_q));  // open: clr
  Register #(.width(32)) register_2 (
    .D(WriteData), .en(demultiplexer_1_out1), .clk(Clk), .Q(register_2_q));  // open: clr
  Register #(.width(32)) register_3 (
    .D(WriteData), .en(demultiplexer_1_out2), .clk(Clk), .Q(register_3_q));  // open: clr
  Register #(.width(32)) register_4 (
    .D(WriteData), .en(demultiplexer_1_out5), .clk(Clk), .Q(register_4_q));  // open: clr
  Register #(.width(32)) register_5 (
    .D(WriteData), .en(demultiplexer_1_out6), .clk(Clk), .Q(register_5_q));  // open: clr
  Register #(.width(32)) register_6 (
    .D(WriteData), .en(demultiplexer_1_out7), .clk(Clk), .Q(register_6_q));  // open: clr
  Register #(.width(32)) register_7 (
    .D(WriteData), .en(demultiplexer_1_out8), .clk(Clk), .Q(register_7_q));  // open: clr
  Register #(.width(32)) register_8 (
    .D(WriteData), .en(demultiplexer_1_out9), .clk(Clk), .Q(register_8_q));  // open: clr
  Register #(.width(32)) register_9 (
    .D(WriteData), .en(demultiplexer_1_out10), .clk(Clk), .Q(register_9_q));  // open: clr
  Multiplexer #(.select(5), .width(32)) multiplexer_1 (
    .in0(register_1_q), .in1(register_2_q), .in2(register_3_q), .in5(register_4_q), .in6(register_5_q),
    .in7(register_6_q), .in8(register_7_q), .in9(register_8_q), .in10(register_9_q), .out(ReadData1),
    .sel(ReadRegister1_rs1));  // open: in3, in4, in11, in12, in13, in14, in15, in16, in17, in18, in19, in20, in21, in22, in23, in24, in25, in26, in27, in28, in29, in30, in31
  Multiplexer #(.select(5), .width(32)) multiplexer_2 (
    .in0(register_1_q), .in1(register_2_q), .in2(register_3_q), .in5(register_4_q), .in6(register_5_q),
    .in7(register_6_q), .in8(register_7_q), .in9(register_8_q), .in10(register_9_q), .out(ReadData2),
    .sel(ReadRegister2_rs2));  // open: in3, in4, in11, in12, in13, in14, in15, in16, in17, in18, in19, in20, in21, in22, in23, in24, in25, in26, in27, in28, in29, in30, in31
endmodule
